// Logisim project Subtracao.circ as structural Verilog: 1 circuit, main circuit main
module main (
  input  [3:0] Entrada_A,
  input  [3:0] Entrada_B,
  input  [1:0] in_3,
  input  [1:0] in_4,
  input  [1:0] in_5,
  input  [1:0] in_6,
  output [3:0] Saida,
  output sinal
);

  wire bitselector_1_out, bitselector_2_out, bitselector_3_out, bitselector_4_out;
  wire [3:0] and_1_out, not_1_out, not_2_out, xor_1_out;

  assign not_1_out = ~Entrada_B;  // NOT_Gate not_1, 4 bits wide
  assign not_2_out = ~Entrada_A;  // NOT_Gate not_2, 4 bits wide
  assign Saida = ~xor_1_out;  // NOT_Gate not_3, 4 bits wide
  assign xor_1_out = Entrada_A ^ not_1_out;  // XOR_Gate xor_1, 4 bits wide
  assign and_1_out = not_2_out & Entrada_B;  // AND_Gate and_1, 4 bits wide
  BitSelector #(.width(4)) bitselector_1 (.in(and_1_out), .out(bitselector_1_out), .sel(in_3));
  BitSelector #(.width(4)) bitselector_2 (.in(and_1_out), .out(bitselector_2_out), .sel(in_4));
  BitSelector #(.width(4)) bitselector_3 (.in(and_1_out), .out(bitselector_3_out), .sel(in_5));
  BitSelector #(.width(4)) bitselector_4 (.in(and_1_out), .out(bitselector_4_out), .sel(in_6));
  or or_1 (sinal, bitselector_1_out, bitselector_2_out, bitselector_3_out, bitselector_4_out);
endmodule
