// Logisim project Trabalho.circ as structural Verilog: 2 circuits, main circuit main
module main (
  input  [15:0] dout,
  input  [1:0] Sel_op1,
  input  Sel_op2,
  input  Wr_acc,
  input  Sel_ula,
  output [15:0] din
);

  wire [15:0] multiplexer_1_out, multiplexer_2_out, ula_1_exit;

  Multiplexer #(.width(16), .enable("false")) multiplexer_1 (
    .in1(dout), .out(multiplexer_1_out), .sel(Sel_op2));  // open: in0
  Multiplexer #(.select(2), .width(16), .enable("false")) multiplexer_2 (
    .in0(ula_1_exit), .in2(dout), .out(multiplexer_2_out), .sel(Sel_op1));  // open: in1, in3
  ula ula_1 (.A(din), .B(multiplexer_1_out), .Selec_ULA(Sel_ula), .Exit(ula_1_exit));
  Register #(.width(16)) register_1 (.D(multiplexer_2_out), .en(Wr_acc), .Q(din));  // open: clk, clr
  ROM rom_1 ();  // open: addr, data, sel
  RAM #(.bus("separate")) ram_1 ();  // open: addr, din, data, str, sel, clk, ld, clr
endmodule

module ula (
  input  [15:0] A,
  input  [15:0] B,
  input  Selec_ULA,
  output [15:0] Exit
);

  wire [15:0] adder_1_out, subtractor_1_out;

  Adder #(.width(16)) adder_1 (.a(A), .b(B), .out(adder_1_out), .cin(1'b0));  // open: cout
  Subtractor #(.width(16)) subtractor_1 (.a(A), .b(B), .out(subtractor_1_out), .bin(1'b0));  // open: bout
  Multiplexer #(.width(16), .enable("false")) multiplexer_1 (
    .in0(adder_1_out), .in1(subtractor_1_out), .out(Exit), .sel(Selec_ULA));
endmodule
